// Logisim project design.circ as structural Verilog: 3 circuits, main circuit main
module main (
);

  logical_operations logical_operations_1 ();  // open: A, B, selector, enable, out
endmodule

module logical_operations (
  input  [31:0] A,
  input  [31:0] B,
  input  [1:0] selector,
  input  enable,
  output [31:0] out
);

  wire [31:0] and_1_out, not_1_out, or_1_out, xor_1_out;

  assign and_1_out = A & B;  // AND_Gate and_1, 32 bits wide
  assign or_1_out = A | B;  // OR_Gate or_1, 32 bits wide
  assign xor_1_out = A ^ B;  // XOR_Gate xor_1, 32 bits wide
  assign not_1_out = ~or_1_out;  // NOT_Gate not_1, 32 bits wide
  Multiplexer #(.select(2), .width(32)) multiplexer_1 (
    .in0(and_1_out), .in1(or_1_out), .in2(not_1_out), .in3(xor_1_out), .out(out), .sel(selector), .en(enable));
endmodule

module zero_detector (
  input  [31:0] _32_bit_Input,
  output zero_bit_flag
);

  nor nor_1 (zero_bit_flag, _32_bit_Input[0], _32_bit_Input[1], _32_bit_Input[2], _32_bit_Input[3], _32_bit_Input[4], _32_bit_Input[5], _32_bit_Input[6], _32_bit_Input[7], _32_bit_Input[8], _32_bit_Input[9], _32_bit_Input[10], _32_bit_Input[11], _32_bit_Input[12], _32_bit_Input[13], _32_bit_Input[14], _32_bit_Input[15], _32_bit_Input[17], _32_bit_Input[18], _32_bit_Input[19], _32_bit_Input[20], _32_bit_Input[21], _32_bit_Input[22], _32_bit_Input[23], _32_bit_Input[24], _32_bit_Input[25], _32_bit_Input[26], _32_bit_Input[27], _32_bit_Input[28], _32_bit_Input[29], _32_bit_Input[30], _32_bit_Input[31], _32_bit_Input[16]);
endmodule
